// Logisim project drugi_domaci.circ as structural Verilog: 1 circuit, main circuit 1705
module _1705 (
  input  x1___16,
  input  x2___8,
  input  x3___4,
  input  x4___2,
  input  x5___1,
  output y
);

  wire nor_1_out, nor_2_out, nor_3_out, nor_4_out, nor_5_out, nor_6_out, nor_7_out, nor_8_out, nor_9_out,
       nor_10_out, nor_11_out, nor_12_out, nor_13_out;

  nor nor_1 (nor_1_out, x1___16, x1___16);
  nor nor_2 (nor_2_out, x4___2, x4___2);
  nor nor_3 (nor_3_out, nor_1_out, nor_1_out);
  nor nor_4 (nor_4_out, x2___8, x2___8);
  nor nor_5 (nor_5_out, nor_3_out, nor_4_out);
  nor nor_6 (nor_6_out, nor_2_out, nor_2_out);
  nor nor_7 (nor_7_out, x5___1, x5___1);
  nor nor_8 (nor_8_out, nor_5_out, nor_5_out);
  nor nor_9 (nor_9_out, x3___4, x3___4);
  nor nor_10 (nor_10_out, nor_6_out, nor_7_out);
  nor nor_11 (nor_11_out, nor_8_out, nor_9_out);
  nor nor_12 (nor_12_out, nor_11_out, nor_11_out);
  nor nor_13 (nor_13_out, nor_10_out, nor_10_out);
  nor nor_14 (y, nor_12_out, nor_13_out);

  // Notes on the sheet:
  //   Datum rođenja: 17.05.
  //   Zbir cifara: 1+7+0+5 = 13
endmodule
